// Logisim project cpu.circ as structural Verilog: 6 circuits, main circuit main
module main (
);

  wire ALU_1_zero, and_1_out, and_2_out, clock_1_out, comparator_1_eq, comparator_2_eq, comparator_3_eq,
       comparator_4_eq, controlUnit_1_alusrc, controlUnit_1_beq, controlUnit_1_bne, controlUnit_1_jal,
       controlUnit_1_jr, controlUnit_1_jump, controlUnit_1_memread, controlUnit_1_memwrite,
       controlUnit_1_regwrite, not_1_out, or_1_out, or_2_out, or_3_out, Reset_out;
  wire [3:0] controlUnit_1_alucontrol;
  wire [4:0] instructionDecoder_1_rd, instructionDecoder_1_rs, instructionDecoder_1_rt_rd, multiplexer_8_out,
       multiplexer_9_out;
  wire [5:0] instructionDecoder_1_opcode;
  wire [10:0] instructionDecoder_1_func;
  wire [23:0] ALU_1_aluresult;
  wire [25:0] PC_q;
  wire [31:0] adder_1_out, adder_2_out, ALU_1_aluresult_2, bit_extender_1_out, bit_extender_2_out,
       multiplexer_1_out, multiplexer_2_out, multiplexer_3_out, multiplexer_4_out, multiplexer_5_out,
       multiplexer_6_out, multiplexer_7_out, multiplexer_10_out, multiplexer_11_out, multiplexer_12_out,
       multiplexer_13_out, PC_q_2, RAM_1_dout, Registers_1_readdata1, Registers_1_readdata2, ROM_1_data,
       shifter_1_out;
  wire [31:16] instructionDecoder_1_imm;

  Clock clock_1 (.out(clock_1_out));
  Button Reset (.out(Reset_out));
  Register #(.width(32)) PC (
    .D(multiplexer_1_out), .en(1'b1), .clk(clock_1_out), .Q({PC_q_2[31:26], PC_q}), .clr(Reset_out));
  Multiplexer #(.width(32)) multiplexer_1 (
    .in0(multiplexer_2_out), .in1(multiplexer_4_out), .out(multiplexer_1_out), .sel(or_1_out));
  Multiplexer #(.width(32)) multiplexer_2 (
    .in0(adder_1_out), .in1(adder_2_out), .out(multiplexer_2_out), .sel(or_2_out));
  Adder #(.width(32)) adder_1 (.a({PC_q_2[31:26], PC_q}), .b(32'h4), .out(adder_1_out));  // open: cin, cout
  Multiplexer #(.width(32)) multiplexer_3 (
    .in0(multiplexer_5_out), .in1(Registers_1_readdata1), .out(multiplexer_3_out), .sel(controlUnit_1_jr));
  Multiplexer #(.width(32)) multiplexer_4 (
    .in0(multiplexer_3_out), .in1(PC_q_2), .out(multiplexer_4_out), .sel(controlUnit_1_jal));
  or or_1 (or_1_out, controlUnit_1_jal, controlUnit_1_jr, controlUnit_1_jump);
  Multiplexer #(.width(32)) multiplexer_5 (
    .in1(PC_q_2), .out(multiplexer_5_out), .sel(controlUnit_1_jump));  // open: in0
  ROM #(.addrWidth(24), .dataWidth(32)) ROM_1 (.addr(PC_q[25:2]), .data(ROM_1_data));
  Comparator #(.width(6)) comparator_1 (
    .a(instructionDecoder_1_opcode), .b(6'b000100), .eq(comparator_1_eq));  // open: gt, lt
  Multiplexer #(.width(32)) multiplexer_6 (
    .in0(multiplexer_13_out), .in1({instructionDecoder_1_imm, {16{1'b0}}}), .out(multiplexer_6_out),
    .sel(comparator_1_eq));
  instructionDecoder instructionDecoder_1 (
    .Inst(ROM_1_data), .Func(instructionDecoder_1_func), .Rd(instructionDecoder_1_rd),
    .Rt_Rd(instructionDecoder_1_rt_rd), .Rs(instructionDecoder_1_rs), .Opcode(instructionDecoder_1_opcode),
    .Imm(instructionDecoder_1_imm), .JumpAddr(PC_q_2[25:0]));
  Multiplexer #(.width(32)) multiplexer_7 (
    .in0(multiplexer_6_out), .in1(adder_1_out), .out(multiplexer_7_out), .sel(controlUnit_1_jal));
  assign bit_extender_1_out = {{16{1'b0}}, instructionDecoder_1_imm};  // Bit_Extender bit_extender_1
  assign bit_extender_2_out = {{16{instructionDecoder_1_imm[31]}}, instructionDecoder_1_imm};  // Bit_Extender bit_extender_2
  Multiplexer #(.width(5)) multiplexer_8 (
    .in0(instructionDecoder_1_rt_rd), .in1(instructionDecoder_1_rd), .out(multiplexer_8_out),
    .sel(comparator_2_eq));
  Comparator #(.width(6)) comparator_2 (
    .a(instructionDecoder_1_opcode), .b({6{1'b0}}), .eq(comparator_2_eq));  // open: gt, lt
  Multiplexer #(.width(5)) multiplexer_9 (
    .in0(multiplexer_8_out), .in1({5{1'b1}}), .out(multiplexer_9_out), .sel(controlUnit_1_jal));
  Multiplexer #(.width(32)) multiplexer_10 (
    .in0(bit_extender_1_out), .in1(bit_extender_2_out), .out(multiplexer_10_out), .sel(or_3_out));
  Multiplexer #(.width(32)) multiplexer_11 (
    .in0(Registers_1_readdata2), .in1(multiplexer_10_out), .out(multiplexer_11_out),
    .sel(controlUnit_1_alusrc));
  Adder #(.width(32)) adder_2 (.a(adder_1_out), .b(bit_extender_2_out), .out(adder_2_out));  // open: cin, cout
  controlUnit controlUnit_1 (
    .Opcode(instructionDecoder_1_opcode), .Func(instructionDecoder_1_func),
    .RegWrite(controlUnit_1_regwrite), .ALUsrc(controlUnit_1_alusrc), .MemRead(controlUnit_1_memread),
    .MemWrite(controlUnit_1_memwrite), .BEQ(controlUnit_1_beq), .BNE(controlUnit_1_bne),
    .Jump(controlUnit_1_jump), .JR(controlUnit_1_jr), .JAL(controlUnit_1_jal),
    .ALUcontrol(controlUnit_1_alucontrol));  // open: MemToReg
  or or_2 (or_2_out, and_1_out, and_2_out);
  Registers Registers_1 (
    .ReadReg2(instructionDecoder_1_rt_rd), .ReadReg1(instructionDecoder_1_rs), .WriteReg(multiplexer_9_out),
    .RegWrite(controlUnit_1_regwrite), .WriteData(multiplexer_7_out), .RST(Reset_out), .CLK(clock_1_out),
    .ReadData2(Registers_1_readdata2), .ReadData1(Registers_1_readdata1));
  ALU ALU_1 (
    .A(Registers_1_readdata1), .B(multiplexer_11_out), .ALUcontrol(controlUnit_1_alucontrol),
    .ALUresult({ALU_1_aluresult_2[31:26], ALU_1_aluresult, ALU_1_aluresult_2[1:0]}), .Zero(ALU_1_zero));
  not not_1 (not_1_out, ALU_1_zero);
  and and_1 (and_1_out, not_1_out, controlUnit_1_bne);
  and and_2 (and_2_out, ALU_1_zero, controlUnit_1_beq);
  Comparator #(.width(4)) comparator_3 (
    .a(controlUnit_1_alucontrol), .b(4'b0000), .eq(comparator_3_eq));  // open: gt, lt
  or or_3 (or_3_out, controlUnit_1_memread, controlUnit_1_memwrite, controlUnit_1_beq, controlUnit_1_bne, comparator_3_eq);
  RAM #(.addrWidth(24), .asyncread("true"), .dataWidth(32)) RAM_1 (
    .addr(ALU_1_aluresult), .we(controlUnit_1_memwrite), .oe(controlUnit_1_memread), .clk(clock_1_out),
    .din(Registers_1_readdata2), .dout(RAM_1_dout));
  Multiplexer #(.width(32)) multiplexer_12 (
    .in0({ALU_1_aluresult_2[31:26], ALU_1_aluresult, ALU_1_aluresult_2[1:0]}), .in1(RAM_1_dout),
    .out(multiplexer_12_out), .sel(controlUnit_1_memread));
  Comparator #(.width(6)) comparator_4 (
    .a(instructionDecoder_1_opcode), .b(6'b000100), .eq(comparator_4_eq));  // open: gt, lt
  Shifter #(.width(32)) shifter_1 (.in(multiplexer_12_out), .\dist (5'b10000), .out(shifter_1_out));
  Multiplexer #(.width(32)) multiplexer_13 (
    .in0(multiplexer_12_out), .in1(shifter_1_out), .out(multiplexer_13_out), .sel(comparator_4_eq));

  // Notes on the sheet:
  //   contents of ROM_1 (hex, n*v repeats v):
  //   7bd0400 4010001 4020001 4140001 415ffff 416000b 1e96003c 68a0001 68b0002 2800005c 5970000 44a0000
  //   6eb0000 2800005c 5820000 42a0000 6eb0000 2800005c 1950800 15a801 6940002 24000018 24000058 7bdfffc
  //   1bbf0000 40c0000 1d60001c 96d0001 1da00004 18a6000 40d0001 14d5005 16d5806 24000068 17bf0000 7bd0004
  //   2fe00000 7bdfffc 1bbf0000 40c0000 40d0000 1d600040 1d40003c 40e0001 411001f 1d17005 4110001 1b16805
  //   14e8002 1e000004 5ad0001 1ab7808 21e00008 1ab6801 18e6003 1d17006 1dc00004 1c00ffd4 17bf0000 7bd0004
  //   2fe00000
  //   LUI
endmodule

module ALU (
  input  [31:0] A,
  input  [31:0] B,
  input  [3:0] ALUcontrol,
  output [31:0] ALUresult,
  output Zero
);

  wire [31:0] adder_1_out, and_1_out, bit_extender_1_out, or_1_out, shifter_1_out, shifter_2_out,
       shifter_3_out, subtractor_1_out, xor_1_out;

  Adder #(.width(32)) adder_1 (.a(A), .b(B), .out(adder_1_out));  // open: cin, cout
  Subtractor #(.width(32)) subtractor_1 (.a(A), .b(B), .out(subtractor_1_out));  // open: bin, bout
  assign and_1_out = A & B;  // AND_Gate and_1, 32 bits wide
  assign or_1_out = A | B;  // OR_Gate or_1, 32 bits wide
  assign xor_1_out = A ^ B;  // XOR_Gate xor_1, 32 bits wide
  Shifter #(.width(32)) shifter_1 (.in(A), .\dist (B[4:0]), .out(shifter_1_out));
  Shifter #(.shift("lr"), .width(32)) shifter_2 (.in(A), .\dist (B[4:0]), .out(shifter_2_out));
  Shifter #(.shift("ar"), .width(32)) shifter_3 (.in(A), .\dist (B[4:0]), .out(shifter_3_out));
  assign bit_extender_1_out = {{31{1'b0}}, subtractor_1_out[31]};  // Bit_Extender bit_extender_1
  Multiplexer #(.select(4), .width(32)) multiplexer_1 (
    .in0(adder_1_out), .in1(subtractor_1_out), .in2(and_1_out), .in3(or_1_out), .in4(xor_1_out),
    .in5(shifter_1_out), .in6(shifter_2_out), .in7(shifter_3_out), .in8(bit_extender_1_out), .out(ALUresult),
    .sel(ALUcontrol));  // open: in9, in10, in11, in12, in13, in14, in15
  nor nor_1 (Zero, ALUresult[0], ALUresult[1], ALUresult[2], ALUresult[3], ALUresult[4], ALUresult[5], ALUresult[6], ALUresult[7], ALUresult[8], ALUresult[9], ALUresult[10], ALUresult[11], ALUresult[12], ALUresult[13], ALUresult[14], ALUresult[15], ALUresult[17], ALUresult[18], ALUresult[19], ALUresult[20], ALUresult[21], ALUresult[22], ALUresult[23], ALUresult[24], ALUresult[25], ALUresult[26], ALUresult[27], ALUresult[28], ALUresult[29], ALUresult[30], ALUresult[31], ALUresult[16]);
endmodule

module Registers (
  input  [4:0] ReadReg2,
  input  [4:0] ReadReg1,
  input  [4:0] WriteReg,
  input  RegWrite,
  input  [31:0] WriteData,
  input  RST,
  input  CLK,
  output [31:0] ReadData2,
  output [31:0] ReadData1
);

  wire decoder_1_out1, decoder_1_out2, decoder_1_out3, decoder_1_out4, decoder_1_out5, decoder_1_out6,
       decoder_1_out7, decoder_1_out8, decoder_1_out9, decoder_1_out10, decoder_1_out11, decoder_1_out12,
       decoder_1_out13, decoder_1_out14, decoder_1_out15, decoder_1_out16, decoder_1_out17, decoder_1_out18,
       decoder_1_out19, decoder_1_out20, decoder_1_out21, decoder_1_out22, decoder_1_out23, decoder_1_out24,
       decoder_1_out25, decoder_1_out26, decoder_1_out27, decoder_1_out28, decoder_1_out29, decoder_1_out30,
       decoder_1_out31;
  wire [31:0] x1_q, x2_q, x3_q, x4_q, x5_q, x6_q, x7_q, x8_q, x9_q, x10_q, x11_q, x12_q, x13_q, x14_q, x15_q,
       x16_q, x17_q, x18_q, x19_q, x20_q, x21_q, x22_q, x23_q, x24_q, x25_q, x26_q, x27_q, x28_q, x29_q,
       x30_q, x31_q;

  Decoder #(.select(5)) decoder_1 (
    .out1(decoder_1_out1), .out2(decoder_1_out2), .out3(decoder_1_out3), .out4(decoder_1_out4),
    .out5(decoder_1_out5), .out6(decoder_1_out6), .out7(decoder_1_out7), .out8(decoder_1_out8),
    .out9(decoder_1_out9), .out10(decoder_1_out10), .out11(decoder_1_out11), .out12(decoder_1_out12),
    .out13(decoder_1_out13), .out14(decoder_1_out14), .out15(decoder_1_out15), .out16(decoder_1_out16),
    .out17(decoder_1_out17), .out18(decoder_1_out18), .out19(decoder_1_out19), .out20(decoder_1_out20),
    .out21(decoder_1_out21), .out22(decoder_1_out22), .out23(decoder_1_out23), .out24(decoder_1_out24),
    .out25(decoder_1_out25), .out26(decoder_1_out26), .out27(decoder_1_out27), .out28(decoder_1_out28),
    .out29(decoder_1_out29), .out30(decoder_1_out30), .out31(decoder_1_out31), .sel(WriteReg), .en(RegWrite));  // open: out0
  Register #(.width(32)) x8 (.D(WriteData), .en(decoder_1_out8), .clk(CLK), .Q(x8_q), .clr(RST));
  Register #(.width(32)) x16 (.D(WriteData), .en(decoder_1_out16), .clk(CLK), .Q(x16_q), .clr(RST));
  Register #(.width(32)) x24 (.D(WriteData), .en(decoder_1_out24), .clk(CLK), .Q(x24_q), .clr(RST));
  Register #(.width(32)) x1 (.D(WriteData), .en(decoder_1_out1), .clk(CLK), .Q(x1_q), .clr(RST));
  Register #(.width(32)) x9 (.D(WriteData), .en(decoder_1_out9), .clk(CLK), .Q(x9_q), .clr(RST));
  Register #(.width(32)) x17 (.D(WriteData), .en(decoder_1_out17), .clk(CLK), .Q(x17_q), .clr(RST));
  Register #(.width(32)) x25 (.D(WriteData), .en(decoder_1_out25), .clk(CLK), .Q(x25_q), .clr(RST));
  Register #(.width(32)) x2 (.D(WriteData), .en(decoder_1_out2), .clk(CLK), .Q(x2_q), .clr(RST));
  Register #(.width(32)) x10 (.D(WriteData), .en(decoder_1_out10), .clk(CLK), .Q(x10_q), .clr(RST));
  Register #(.width(32)) x18 (.D(WriteData), .en(decoder_1_out18), .clk(CLK), .Q(x18_q), .clr(RST));
  Register #(.width(32)) x26 (.D(WriteData), .en(decoder_1_out26), .clk(CLK), .Q(x26_q), .clr(RST));
  Register #(.width(32)) x11 (.D(WriteData), .en(decoder_1_out11), .clk(CLK), .Q(x11_q), .clr(RST));
  Register #(.width(32)) x3 (.D(WriteData), .en(decoder_1_out3), .clk(CLK), .Q(x3_q), .clr(RST));
  Register #(.width(32)) x19 (.D(WriteData), .en(decoder_1_out19), .clk(CLK), .Q(x19_q), .clr(RST));
  Register #(.width(32)) x27 (.D(WriteData), .en(decoder_1_out27), .clk(CLK), .Q(x27_q), .clr(RST));
  Register #(.width(32)) x4 (.D(WriteData), .en(decoder_1_out4), .clk(CLK), .Q(x4_q), .clr(RST));
  Register #(.width(32)) x12 (.D(WriteData), .en(decoder_1_out12), .clk(CLK), .Q(x12_q), .clr(RST));
  Register #(.width(32)) x20 (.D(WriteData), .en(decoder_1_out20), .clk(CLK), .Q(x20_q), .clr(RST));
  Register #(.width(32)) x28 (.D(WriteData), .en(decoder_1_out28), .clk(CLK), .Q(x28_q), .clr(RST));
  Register #(.width(32)) x5 (.D(WriteData), .en(decoder_1_out5), .clk(CLK), .Q(x5_q), .clr(RST));
  Register #(.width(32)) x13 (.D(WriteData), .en(decoder_1_out13), .clk(CLK), .Q(x13_q), .clr(RST));
  Register #(.width(32)) x21 (.D(WriteData), .en(decoder_1_out21), .clk(CLK), .Q(x21_q), .clr(RST));
  Register #(.width(32)) x29 (.D(WriteData), .en(decoder_1_out29), .clk(CLK), .Q(x29_q), .clr(RST));
  Register #(.width(32)) x14 (.D(WriteData), .en(decoder_1_out14), .clk(CLK), .Q(x14_q), .clr(RST));
  Register #(.width(32)) x6 (.D(WriteData), .en(decoder_1_out6), .clk(CLK), .Q(x6_q), .clr(RST));
  Register #(.width(32)) x22 (.D(WriteData), .en(decoder_1_out22), .clk(CLK), .Q(x22_q), .clr(RST));
  Register #(.width(32)) x30 (.D(WriteData), .en(decoder_1_out30), .clk(CLK), .Q(x30_q), .clr(RST));
  Register #(.width(32)) x7 (.D(WriteData), .en(decoder_1_out7), .clk(CLK), .Q(x7_q), .clr(RST));
  Register #(.width(32)) x15 (.D(WriteData), .en(decoder_1_out15), .clk(CLK), .Q(x15_q), .clr(RST));
  Register #(.width(32)) x23 (.D(WriteData), .en(decoder_1_out23), .clk(CLK), .Q(x23_q), .clr(RST));
  Register #(.width(32)) x31 (.D(WriteData), .en(decoder_1_out31), .clk(CLK), .Q(x31_q), .clr(RST));
  Multiplexer #(.select(5), .width(32)) multiplexer_1 (
    .in0({32{1'b0}}), .in1(x1_q), .in2(x2_q), .in3(x3_q), .in4(x4_q), .in5(x5_q), .in6(x6_q), .in7(x7_q),
    .in8(x8_q), .in9(x9_q), .in10(x10_q), .in11(x11_q), .in12(x12_q), .in13(x13_q), .in14(x14_q),
    .in15(x15_q), .in16(x16_q), .in17(x17_q), .in18(x18_q), .in19(x19_q), .in20(x20_q), .in21(x21_q),
    .in22(x22_q), .in23(x23_q), .in24(x24_q), .in25(x25_q), .in26(x26_q), .in27(x27_q), .in28(x28_q),
    .in29(x29_q), .in30(x30_q), .in31(x31_q), .out(ReadData1), .sel(ReadReg1));
  Multiplexer #(.select(5), .width(32)) multiplexer_2 (
    .in0({32{1'b0}}), .in1(x1_q), .in2(x2_q), .in3(x3_q), .in4(x4_q), .in5(x5_q), .in6(x6_q), .in7(x7_q),
    .in8(x8_q), .in9(x9_q), .in10(x10_q), .in11(x11_q), .in12(x12_q), .in13(x13_q), .in14(x14_q),
    .in15(x15_q), .in16(x16_q), .in17(x17_q), .in18(x18_q), .in19(x19_q), .in20(x20_q), .in21(x21_q),
    .in22(x22_q), .in23(x23_q), .in24(x24_q), .in25(x25_q), .in26(x26_q), .in27(x27_q), .in28(x28_q),
    .in29(x29_q), .in30(x30_q), .in31(x31_q), .out(ReadData2), .sel(ReadReg2));
endmodule

module instructionDecoder (
  input  [31:0] Inst,
  output [10:0] Func,
  output [4:0] Rd,
  output [4:0] Rt_Rd,
  output [4:0] Rs,
  output [5:0] Opcode,
  output [15:0] Imm,
  output [25:0] JumpAddr
);


  assign Func = Inst[10:0];
  assign Imm = Inst[15:0];
  assign JumpAddr = Inst[25:0];
  assign Opcode = Inst[31:26];
  assign Rd = Inst[15:11];
  assign Rs = Inst[25:21];
  assign Rt_Rd = Inst[20:16];
endmodule

module controlUnit (
  input  [5:0] Opcode,
  input  [10:0] Func,
  output RegWrite,
  output ALUsrc,
  output MemRead,
  output MemWrite,
  output MemToReg,
  output BEQ,
  output BNE,
  output Jump,
  output JR,
  output JAL,
  output [3:0] ALUcontrol
);

  wire or_1_out, or_2_out;
  wire [3:0] ALUdecoder_1_alucontrol, multiplexer_1_out;
  wire [15:10] ROM_1_data;

  ROM #(.addrWidth(6), .dataWidth(16)) ROM_1 (
    .addr(Opcode), .data({ROM_1_data, JAL, JR, Jump, BNE, BEQ, MemToReg, MemWrite, MemRead, ALUsrc, RegWrite}));
  ALUdecoder ALUdecoder_1 (.Func(Func), .ALUop(ROM_1_data[12:10]), .ALUcontrol(ALUdecoder_1_alucontrol));
  or or_1 (or_1_out, MemRead, MemWrite);
  or or_2 (or_2_out, BEQ, BNE);
  Multiplexer #(.width(4)) multiplexer_1 (
    .in0(ALUdecoder_1_alucontrol), .in1(4'b0001), .out(multiplexer_1_out), .sel(or_2_out));
  Multiplexer #(.width(4)) multiplexer_2 (.in0(multiplexer_1_out), .in1(4'b0000), .out(ALUcontrol), .sel(or_1_out));

  // Notes on the sheet:
  //   contents of ROM_1 (hex, n*v repeats v):
  //   1 403 c03 1003 1803 417 40a 1020 1040 80 201 100
endmodule

module ALUdecoder (
  input  [10:0] Func,
  input  [2:0] ALUop,
  output [3:0] ALUcontrol
);

  wire [10:0] bit_extender_1_out, multiplexer_1_out, subtractor_1_out;

  assign bit_extender_1_out = {{8{1'b0}}, ALUop};  // Bit_Extender bit_extender_1
  Subtractor #(.width(11)) subtractor_1 (.a(bit_extender_1_out), .b(11'h1), .out(subtractor_1_out));  // open: bin, bout
  Multiplexer #(.select(3), .width(11)) multiplexer_1 (
    .in0(Func), .in1(subtractor_1_out), .in2(subtractor_1_out), .in3(subtractor_1_out),
    .in4(subtractor_1_out), .in5(subtractor_1_out), .in6(subtractor_1_out), .out(multiplexer_1_out),
    .sel(ALUop));  // open: in7
  Bit_Extender #(.in_width(11), .out_width(4), .\type ("zero")) bit_extender_2 (
    .in(multiplexer_1_out), .out(ALUcontrol));
endmodule
